# Fritzing sketch Ultrasonic_Pink_Panther_Doorbell (saved by Fritzing 0.9.3b)
breadboards: 1

parts:
  M1 = DOIT Esp32 DevKit v1 (30 pins long, 11 pins width) [part_number=ESP32S-PIN30]
  J1 = Piezo Speaker
  LED2 = LED - 5mm [color="Red (633nm)" package="5 mm [THT]"]
  LED1 = smd LED [color="Green (555nm)" package="1206 [SMD]"]
  HC-SR04_Sensor_1 = HC-SR04 Ultrasonic Distance Sensor

nets:
  N1: M1.D5, HC-SR04_Sensor_1.TRIG
  N2: M1.D18, J1.pin2
  N3: M1.D19, HC-SR04_Sensor_1.ECHO
  N4: M1.D14, LED2.anode
  N5: M1.D13, LED1.anode
  GND: M1.GND, J1.pin1, LED2.cathode, LED1.cathode, HC-SR04_Sensor_1.GND
  VIN: M1.VIN, HC-SR04_Sensor_1.VCC

custom parts:
  DOIT Esp32 DevKit v1 (30 pins long, 11 pins width): The DOIT Esp32 DevKit v1 is one of the development board created by DOIT to evaluate the ESP-WROOM-32 module. It is based on the ESP32 microcontroller that boasts Wifi, Bluetooth, Ethernet and Low Power support all in a single chip. (vanepp) made breadboard work, adjusted pin numbering and labels and reduced size of schematic and cleaned up pcb. This chip is 30pins long (2 x15) and 11 pins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

// code stored in the sketch: PinkPantherUltrosonic.ino
// Include the necessary libraries
#include <Wire.h>

// Define the ultrasonic sensor pins
const int trigPin = 5;
const int echoPin = 19;

// Define the buzzer pin
#define buzzer 18
// Define the LED pins
#define GREEN_LED 13
#define RED_LED 14

// Define the sound speed in cm/uS
#define SOUND_SPEED 0.034

// Define the maximum distance for the buzzer to turn on
#define MAX_DISTANCE 15

// Other definitions and variables from PinkPantherSong.ino go here...
#define NOTE_B0  31
#define NOTE_C1  33
#define NOTE_CS1 35
#define NOTE_D1  37
#define NOTE_DS1 39
#define NOTE_E1  41
#define NOTE_F1  44
#define NOTE_FS1 46
#define NOTE_G1  49
#define NOTE_GS1 52
#define NOTE_A1  55
#define NOTE_AS1 58
#define NOTE_B1  62
#define NOTE_C2  65
#define NOTE_CS2 69
#define NOTE_D2  73
#define NOTE_DS2 78
#define NOTE_E2  82
#define NOTE_F2  87
#define NOTE_FS2 93
#define NOTE_G2  98
#define NOTE_GS2 104
#define NOTE_A2  110
#define NOTE_AS2 117
#define NOTE_B2  123
#define NOTE_C3  131
#define NOTE_CS3 139
#define NOTE_D3  147
#define NOTE_DS3 156
#define NOTE_E3  165
#define NOTE_F3  175
#define NOTE_FS3 185
#define NOTE_G3  196
#define NOTE_GS3 208
#define NOTE_A3  220
#define NOTE_AS3 233
#define NOTE_B3  247
#define NOTE_C4  262
#define NOTE_CS4 277
#define NOTE_D4  294
#define NOTE_DS4 311
#define NOTE_E4  330
#define NOTE_F4  349
#define NOTE_FS4 370
#define NOTE_G4  392
#define NOTE_GS4 415
#define NOTE_A4  440
#define NOTE_AS4 466
#define NOTE_B4  494
#define NOTE_C5  523
#define NOTE_CS5 554
#define NOTE_D5  587
#define NOTE_DS5 622
#define NOTE_E5  659
#define NOTE_F5  698
#define NOTE_FS5 740
#define NOTE_G5  784
#define NOTE_GS5 831
#define NOTE_A5  880
#define NOTE_AS5 932
#define NOTE_B5  988
#define NOTE_C6  1047
#define NOTE_CS6 1109
#define NOTE_D6  1175
#define NOTE_DS6 1245
#define NOTE_E6  1319
#define NOTE_F6  1397
#define NOTE_FS6 1480
#define NOTE_G6  1568
#define NOTE_GS6 1661
#define NOTE_A6  1760
#define NOTE_AS6 1865
#define NOTE_B6  1976
#define NOTE_C7  2093
#define NOTE_CS7 2217
#define NOTE_D7  2349
#define NOTE_DS7 2489
#define NOTE_E7  2637
#define NOTE_F7  2794
#define NOTE_FS7 2960
#define NOTE_G7  3136
#define NOTE_GS7 3322
#define NOTE_A7  3520
#define NOTE_AS7 3729
#define NOTE_B7  3951
#define NOTE_C8  4186
#define NOTE_CS8 4435
#define NOTE_D8  4699
#define NOTE_DS8 4978
#define REST      0
#define CHANNEL 0 // You can choose any channel from 0 to 15



// Add a variable to keep track of the button state
bool isPlaying = false;

// change this to make the song slower or faster
int tempo = 120;

// // change this to whichever pin you want to use
// int buzzer = 18;

// notes of the moledy followed by the duration.
// a 4 means a quarter note, 8 an eighteenth , 16 sixteenth, so on
// !!negative numbers are used to represent dotted notes,
// so -4 means a dotted quarter note, that is, a quarter plus an eighteenth!!
int melody[] = {

  // Pink Panther theme
  // Score available at https://musescore.com/benedictsong/the-pink-panther
  // Theme by Masato Nakamura, arranged by Teddy Mason

  REST,2, REST,4, REST,8, NOTE_DS4,8, 
  NOTE_E4,-4, REST,8, NOTE_FS4,8, NOTE_G4,-4, REST,8, NOTE_DS4,8,
  NOTE_E4,-8, NOTE_FS4,8,  NOTE_G4,-8, NOTE_C5,8, NOTE_B4,-8, NOTE_E4,8, NOTE_G4,-8, NOTE_B4,8,   
  NOTE_AS4,2, NOTE_A4,-16, NOTE_G4,-16, NOTE_E4,-16, NOTE_D4,-16, 
  NOTE_E4,2, REST,4, REST,8, NOTE_DS4,4,

  NOTE_E4,-4, REST,8, NOTE_FS4,8, NOTE_G4,-4, REST,8, NOTE_DS4,8,
  NOTE_E4,-8, NOTE_FS4,8,  NOTE_G4,-8, NOTE_C5,8, NOTE_B4,-8, NOTE_G4,8, NOTE_B4,-8, NOTE_E5,8,
  NOTE_DS5,1,   
  NOTE_D5,2, REST,4, REST,8, NOTE_DS4,8, 
  NOTE_E4,-4, REST,8, NOTE_FS4,8, NOTE_G4,-4, REST,8, NOTE_DS4,8,
  NOTE_E4,-8, NOTE_FS4,8,  NOTE_G4,-8, NOTE_C5,8, NOTE_B4,-8, NOTE_E4,8, NOTE_G4,-8, NOTE_B4,8,   
  
  NOTE_AS4,2, NOTE_A4,-16, NOTE_G4,-16, NOTE_E4,-16, NOTE_D4,-16, 
  NOTE_E4,-4, REST,4,
  REST,4, NOTE_E5,-8, NOTE_D5,8, NOTE_B4,-8, NOTE_A4,8, NOTE_G4,-8, NOTE_E4,-8,
  NOTE_AS4,16, NOTE_A4,-8, NOTE_AS4,16, NOTE_A4,-8, NOTE_AS4,16, NOTE_A4,-8, NOTE_AS4,16, NOTE_A4,-8,   
  NOTE_G4,-16, NOTE_E4,-16, NOTE_D4,-16, NOTE_E4,16, NOTE_E4,16, NOTE_E4,2,
 
};

// sizeof gives the number of bytes, each int value is composed of two bytes (16 bits)
// there are two values per note (pitch and duration), so for each note there are four bytes
int notes = sizeof(melody) / sizeof(melody[0]) / 2;

// this calculates the duration of a whole note in ms
int wholenote = (60000 * 4) / tempo;

int divider = 0, noteDuration = 0;


void setup() {
  // Initialize the serial communication
  Serial.begin(115200);

  // Set the ultrasonic sensor pins
  pinMode(trigPin, OUTPUT);
  pinMode(echoPin, INPUT);

    // Set the LED pins
  pinMode(GREEN_LED, OUTPUT);
  pinMode(RED_LED, OUTPUT);

  // Initialize the LEDC peripheral
  ledcSetup(CHANNEL, 2000, 8); // 2000 Hz PWM, 8-bit resolution
  ledcAttachPin(buzzer, CHANNEL);
}

void loop() {
  // Measure the distance
  digitalWrite(trigPin, LOW);
  delayMicroseconds(2);
  digitalWrite(trigPin, HIGH);
  delayMicroseconds(10);
  digitalWrite(trigPin, LOW);
  long duration = pulseIn(echoPin, HIGH);
  float distanceCm = duration * SOUND_SPEED / 2;

  // Print the distance
  Serial.print("Distance (cm): ");
  Serial.println(distanceCm);

  // If the distance is less than the maximum distance, play the melody
  if (distanceCm < MAX_DISTANCE) {
    digitalWrite(GREEN_LED, HIGH); // Turn on the green LED
    digitalWrite(RED_LED, LOW); // Turn off the red LED
    playMelody();
  } else {
     digitalWrite(GREEN_LED, LOW); // Turn off the green LED
    digitalWrite(RED_LED, HIGH); // Turn on the red LED
    noTone(buzzer);
  }

  delay(500); // Log the distances every 2 seconds | update: 500 ms
}

// Add a variable to keep track of the last time the LED state was changed
unsigned long lastLedChange = 0;

// Add a variable to control the LED flashing speed
int ledInterval = 200; // The LED will change state every 200 ms

// // playMelody function from PinkPantherSong.ino goes here...
// void playMelody(){
//   // iterate over the notes of the melody.
//   // Remember, the array is twice the number of notes (notes + durations)
//   for (int thisNote = 0; thisNote < notes * 2; thisNote = thisNote + 2) {

//     // calculates the duration of each note
//     divider = melody[thisNote + 1];
//     if (divider > 0) {
//       // regular note, just proceed
//       noteDuration = (wholenote) / divider;
//     } else if (divider < 0) {
//       // dotted notes are represented with negative durations!!
//       noteDuration = (wholenote) / abs(divider);
//       noteDuration *= 1.5; // increases the duration in half for dotted notes
//     }

//     // we only play the note for 90% of the duration, leaving 10% as a pause
//     tone(buzzer, melody[thisNote], noteDuration * 0.9);

//    // Flash the green LED on and off while the note is playing
//     if (millis() - lastLedChange > ledInterval) {
//       // If enough time has passed, change the state of the LED
//       digitalWrite(GREEN_LED, !digitalRead(GREEN_LED));
//       lastLedChange = millis();
//     }

//     // Wait for the specief duration before playing the next note.
//     delay(noteDuration);

//     // stop the waveform generation before the next note.
//     noTone(buzzer);

//     // Measure the distance
//     digitalWrite(trigPin, LOW);
//     delayMicroseconds(2);
//     digitalWrite(trigPin, HIGH);
//     delayMicroseconds(10);
//     digitalWrite(trigPin, LOW);
//     long duration = pulseIn(echoPin, HIGH);
//     float distanceCm = duration * SOUND_SPEED / 2;

//     // If the distance is more than the maximum distance, stop the melody
//     if (distanceCm > MAX_DISTANCE) {
//       break;
//     }
//   }
// }

void playMelody() {
  // iterate over the notes of the melody.
  // Remember, the array is twice the number of notes (notes + durations)
  for (int thisNote = 0; thisNote < notes * 2; thisNote = thisNote + 2) {

    // Measure the distance
    digitalWrite(trigPin, LOW);
    delayMicroseconds(2);
    digitalWrite(trigPin, HIGH);
    delayMicroseconds(10);
    digitalWrite(trigPin, LOW);
    long duration = pulseIn(echoPin, HIGH);
    float distanceCm = duration * SOUND_SPEED / 2;

    // If the distance is more than the maximum distance, stop the melody
    if (distanceCm > MAX_DISTANCE) {
      break;
    }

    // calculates the duration of each note
    divider = melody[thisNote + 1];
    if (divider > 0) {
      // regular note, just proceed
      noteDuration = (wholenote) / divider;
    } else if (divider < 0) {
      // dotted notes are represented with negative durations!!
      noteDuration = (wholenote) / abs(divider);
      noteDuration *= 1.5; // increases the duration in half for dotted notes
    }

    // we only play the note for 90% of the duration, leaving 10% as a pause
    tone(buzzer, melody[thisNote], noteDuration * 0.9);

    // Flash the green LED on and off while the note is playing
    if (millis() - lastLedChange > ledInterval) {
      // If enough time has passed, change the state of the LED
      digitalWrite(GREEN_LED, !digitalRead(GREEN_LED));
      lastLedChange = millis();
    }

    // Wait for the specief duration before playing the next note.
    delay(noteDuration);

    // stop the waveform generation before the next note.
    noTone(buzzer);
  }
}
